# Fritzing sketch schematic (saved by Fritzing 0.9.2b)
breadboards: 1

parts:
  Teensy = Teensy 2.0
  C1 = Electrolytic Capacitor [capacitance=1µF package="100 mil [THT, electrolytic]"]
  R1 = Resistor [tolerance=±5% resistance=470 package=THT]
  Clock = IC, DIP package, 4 pins [chip_label=Clock]
  TRS1 = Audio Jack (TRS) 3.5mm [package="4Ucon 08780 [THT]"]
  LED1 = LED - 5mm [color="Red (633nm)" package="5 mm [THT]"]
  LED2 = LED - 5mm [color="Red (633nm)" package="5 mm [THT]"]
  LED3 = LED - 5mm [color="Red (633nm)" package="5 mm [THT]"]
  LED4 = LED - 5mm [color="Red (633nm)" package="5 mm [THT]"]
  R3 = Resistor [tolerance=±5% resistance=220 package=THT]
  R4 = Resistor [tolerance=±5% resistance=220 package=THT]
  R5 = Resistor [tolerance=±5% resistance=220 package=THT]
  R6 = Resistor [tolerance=±5% resistance=220 package=THT]
  SN76489 = IC, DIP package, 16 pins [chip_label=SN76489]

nets:
  N1: Teensy.GND, Clock.pin3, TRS1.Sleeve, R3.Pin_1, R4.Pin_1, R5.Pin_1, R6.Pin_1, SN76489.pin6, SN76489.pin8
  N2: Teensy.B0, SN76489.pin10
  N3: Teensy.B1, SN76489.pin11
  N4: Teensy.B2, SN76489.pin12
  N5: Teensy.B3, SN76489.pin13
  N6: Teensy.B7, SN76489.pin3
  N7: Teensy.D0, LED1.anode
  N8: Teensy.C6, LED2.anode
  N9: Teensy.C7, LED3.anode
  N10: Teensy.VCC, Clock.pin1, SN76489.pin16
  N11: Teensy.D7, LED4.anode
  N12: Teensy.B4, SN76489.pin15
  N13: Teensy.B5, SN76489.pin1
  N14: Teensy.B6, SN76489.pin2
  N15: Teensy.F0, SN76489.pin5
  N16: C1.-, R1.Pin_0
  N17: C1.+, SN76489.pin7
  N18: R1.Pin_1, TRS1.Ring, TRS1.Tip
  N19: Clock.pin4, SN76489.pin14
  N20: LED1.cathode, R6.Pin_0
  N21: LED2.cathode, R5.Pin_0
  N22: LED3.cathode, R4.Pin_0
  N23: LED4.cathode, R3.Pin_0
